// Logisim project ProyectoIntegrador.circ as structural Verilog
module Controlador_Entrada (
  input  Boton_1,
  input  Boton_2,
  input  Boton_3,
  input  Boton_4,
  input  Boton_5,
  input  Boton_6,
  input  Boton_7,
  input  Boton_8,
  input  Boton_9,
  input  Boton_RESET,
  output [1:0] Boton_1_star,
  output [1:0] Boton_2_star,
  output [1:0] Boton_3_star,
  output [1:0] Boton_4_star,
  output [1:0] Boton_5_star,
  output [1:0] Boton_6_star,
  output [1:0] Boton_7_star,
  output [1:0] Boton_8_star,
  output [1:0] Boton_9_star,
  output Bandera_Turno,
  output Victoria
);

  wire boton_1_triggered, boton_2_triggered, boton_3_triggered, boton_4_triggered, boton_5_triggered,
       boton_6_triggered, boton_7_triggered, boton_8_triggered, boton_9_triggered, xor_1_out, xor_2_out,
       xor_3_out, xor_4_out, xor_5_out, xor_6_out, xor_7_out;

  Boton u_boton_1 (
    .TRIGGER(Boton_1), .RESET(Boton_RESET), .TURNO(Bandera_Turno), .VALOR(Boton_1_star),
    .TRIGGERED(boton_1_triggered), .VICTORIA(1'b0));
  Boton u_boton_2 (
    .TRIGGER(Boton_2), .RESET(Boton_RESET), .TURNO(Bandera_Turno), .VALOR(Boton_2_star),
    .TRIGGERED(boton_2_triggered), .VICTORIA(1'b0));
  Boton u_boton_3 (
    .TRIGGER(Boton_3), .RESET(Boton_RESET), .TURNO(Bandera_Turno), .VALOR(Boton_3_star),
    .TRIGGERED(boton_3_triggered), .VICTORIA(1'b0));
  Boton u_boton_4 (
    .TRIGGER(Boton_4), .RESET(Boton_RESET), .TURNO(Bandera_Turno), .VALOR(Boton_4_star),
    .TRIGGERED(boton_4_triggered), .VICTORIA(1'b0));
  Boton u_boton_5 (
    .TRIGGER(Boton_5), .RESET(Boton_RESET), .TURNO(Bandera_Turno), .VALOR(Boton_5_star),
    .TRIGGERED(boton_5_triggered), .VICTORIA(1'b0));
  Boton u_boton_6 (
    .TRIGGER(Boton_6), .RESET(Boton_RESET), .TURNO(Bandera_Turno), .VALOR(Boton_6_star),
    .TRIGGERED(boton_6_triggered), .VICTORIA(1'b0));
  Boton u_boton_7 (
    .TRIGGER(Boton_7), .RESET(Boton_RESET), .TURNO(Bandera_Turno), .VALOR(Boton_7_star),
    .TRIGGERED(boton_7_triggered), .VICTORIA(1'b0));
  Boton u_boton_8 (
    .TRIGGER(Boton_8), .RESET(Boton_RESET), .TURNO(Bandera_Turno), .VALOR(Boton_8_star),
    .TRIGGERED(boton_8_triggered), .VICTORIA(1'b0));
  Boton u_boton_9 (
    .TRIGGER(Boton_9), .RESET(Boton_RESET), .TURNO(Bandera_Turno), .VALOR(Boton_9_star),
    .TRIGGERED(boton_9_triggered), .VICTORIA(1'b0));
  xor xor_1 (xor_1_out, boton_1_triggered, boton_2_triggered);
  xor xor_2 (xor_2_out, boton_3_triggered, boton_4_triggered);
  xor xor_3 (xor_3_out, boton_5_triggered, boton_6_triggered);
  xor xor_4 (xor_4_out, boton_7_triggered, boton_8_triggered);
  xor xor_5 (xor_5_out, xor_1_out, xor_2_out);
  xor xor_6 (xor_6_out, xor_3_out, xor_4_out);
  xor xor_7 (xor_7_out, xor_5_out, xor_6_out);
  xor xor_8 (Bandera_Turno, xor_7_out, boton_9_triggered);

  // Notes on the sheet:
  //   Entrada
  //   Salida
endmodule

module Controlador_Salida (
  input  [1:0] Boton_1_star,
  input  [1:0] Boton_2_star,
  input  [1:0] Boton_3_star,
  input  [1:0] Boton_4_star,
  input  [1:0] Boton_5_star,
  input  [1:0] Boton_6_star,
  input  [1:0] Boton_7_star,
  input  [1:0] Boton_8_star,
  input  [1:0] Boton_9_star,
  input  Bandera_Turno,
  input  Victoria
);


  // Notes on the sheet:
  //   Entrada
endmodule

module Boton (
  input  TRIGGER,
  input  RESET,
  input  TURNO,
  input  VICTORIA,
  output [1:0] VALOR,
  output TRIGGERED
);

  wire d_ff_2_q, d_ff_3_q, demultiplexer_1_out1, multiplexer_1_out, not_1_out, or_1_out;
  wire [0:0] demultiplexer_1_out0;
  wire [1:0] multiplexer_3_out;

  Multiplexer #(.enable("false")) multiplexer_1 (.in0(TRIGGER), .in1(1'b0), .out(multiplexer_1_out), .sel(VICTORIA));
  D_Flip_Flop d_ff_1 (
    .clk(multiplexer_1_out), .D(multiplexer_1_out), .Q(TRIGGERED), .reset(RESET));  // open: Qn, preset
  not not_1 (not_1_out, TURNO);
  D_Flip_Flop d_ff_2 (.clk(TRIGGERED), .D(not_1_out), .Q(d_ff_2_q), .reset(RESET));  // open: Qn, preset
  D_Flip_Flop d_ff_3 (.clk(TRIGGERED), .D(TURNO), .Q(d_ff_3_q), .reset(RESET));  // open: Qn, preset
  Demultiplexer #(.enable("false")) demultiplexer_1 (
    .out0(demultiplexer_1_out0[0]), .out1(demultiplexer_1_out1), .in(d_ff_2_q), .sel(or_1_out));
  or or_1 (or_1_out, d_ff_2_q, d_ff_3_q);
  Multiplexer #(.width(2), .enable("false")) multiplexer_2 (
    .in0({1'b0, demultiplexer_1_out0[0]}), .in1(multiplexer_3_out), .out(VALOR), .sel(or_1_out));
  Multiplexer #(.width(2), .enable("false")) multiplexer_3 (
    .in0(2'b10), .in1(2'b01), .out(multiplexer_3_out), .sel(demultiplexer_1_out1));

  // Notes on the sheet:
  //   Entrada
  //   Salida
endmodule
